// Logisim project Lab4LotsOfGates.circ as structural Verilog: 1 circuit, main circuit main
module main (
  input  a,
  input  b,
  input  c,
  output x,
  output y,
  output xx,
  output yy
);

  wire and_1_out, and_2_out, and_3_out, nor_1_out, nor_2_out, not_1_out, not_2_out, not_3_out, not_4_out,
       not_5_out, or_1_out, or_2_out;

  not not_1 (not_1_out, a);
  not not_2 (not_2_out, b);
  not not_3 (not_3_out, c);
  not not_4 (not_4_out, not_2_out);
  not not_5 (not_5_out, not_3_out);
  and and_1 (and_1_out, ~a, ~b);  // AND_Gate
  nor nor_1 (nor_1_out, ~b, ~c);  // NOR_Gate
  and and_2 (and_2_out, not_1_out, not_2_out);
  nor nor_2 (nor_2_out, not_2_out, not_3_out);
  or or_1 (or_1_out, and_1_out, nor_1_out);
  nand nand_1 (y, b, c);
  and and_3 (and_3_out, not_4_out, not_5_out);
  not not_6 (yy, and_3_out);
  not not_7 (x, or_1_out);
  not not_8 (xx, or_2_out);
  or or_2 (or_2_out, and_2_out, nor_2_out);
endmodule
