// Logisim project TwoIdenticalCircuits.circ as structural Verilog: 3 circuits, main circuit main
module main (
  input  SW_1,
  input  SW_2,
  input  SW_3,
  output out_4,
  output out_5
);

  wire and_2_out, nand_1_out, nor_1_out, or_1_out;

  and and_1 (out_4, SW_1, SW_2, ~SW_3);  // AND_Gate
  and and_2 (and_2_out, SW_1, SW_2);
  or or_1 (or_1_out, and_2_out, nor_1_out);
  nor nor_1 (nor_1_out, ~SW_2, ~SW_3);  // NOR_Gate
  nand nand_1 (nand_1_out, SW_2, SW_3);
  and and_3 (out_5, or_1_out, nand_1_out);
endmodule

module x (
  input  SW1,
  input  SW2,
  input  SW3,
  output x,
  output y
);

  wire and_2_out, nand_1_out, nor_1_out, not_1_out, not_2_out, not_3_out, or_1_out;

  not not_1 (not_1_out, SW3);
  not not_2 (not_2_out, SW2);
  not not_3 (not_3_out, SW3);
  and and_1 (x, SW1, SW2, not_1_out);
  and and_2 (and_2_out, SW1, SW2);
  nor nor_1 (nor_1_out, not_2_out, not_3_out);
  or or_1 (or_1_out, and_2_out, nor_1_out);
  nand nand_1 (nand_1_out, SW2, SW3);
  and and_3 (y, or_1_out, nand_1_out);
endmodule

module y (
  input  SW1,
  input  SW2,
  input  SW3,
  output x,
  output y
);

  wire not_1_out, not_2_out;

  not not_1 (not_1_out, SW3);
  not not_2 (not_2_out, SW3);
  and and_1 (x, SW1, SW2, not_1_out);
  and and_2 (y, SW1, SW2, not_2_out);
endmodule
